// Logisim project cpu.circ as structural Verilog: 6 circuits, main circuit d-latch
module d_latch (
  input  enabler,
  input  \input ,
  output Q,
  output Q_prime
);

  wire and_1_out, and_2_out, not_1_out;

  not not_1 (not_1_out, \input );
  and and_1 (and_1_out, not_1_out, enabler);
  and and_2 (and_2_out, enabler, \input );
  nor nor_1 (Q, and_1_out, Q_prime);
  nor nor_2 (Q_prime, Q, and_2_out);
endmodule

module d_flip_flop (
  input  d,
  output q,
  output q_prime
);

  wire clk_out, d_latch_1_q_prime, not_1_out, not_2_out;

  Clock clk (.out(clk_out));
  d_latch d_latch_1 (.Q_prime(d_latch_1_q_prime), .\input (d), .enabler(not_1_out));  // open: Q
  not not_1 (not_1_out, clk_out);
  not not_2 (not_2_out, not_1_out);
  d_latch d_latch_2 (.Q(q), .Q_prime(q_prime), .\input (d_latch_1_q_prime), .enabler(not_2_out));
endmodule

module full_adder_1_bit (
  input  input_1_1_bit,
  input  input_2_1_bit,
  input  carry_in,
  output carry_out,
  output result
);

  wire and_1_out, and_2_out, and_3_out;

  and and_1 (and_1_out, input_1_1_bit, input_2_1_bit);
  and and_2 (and_2_out, input_2_1_bit, carry_in);
  and and_3 (and_3_out, input_1_1_bit, carry_in);
  ExactlyOne xor_1 (.out(result), .in0(input_1_1_bit), .in1(input_2_1_bit), .in2(carry_in));
  or or_1 (carry_out, and_1_out, and_2_out, and_3_out);
endmodule

module full_adder_4_bit (
  input  [3:0] input1_4_bit,
  input  [3:0] input2_4_bit,
  input  carry_in,
  output carry_out,
  output [3:0] \output 
);

  wire full_adder_1_bit_2_carry_out, full_adder_1_bit_3_carry_out, full_adder_1_bit_4_carry_out;

  full_adder_1_bit full_adder_1_bit_1 (
    .input_1_1_bit(input1_4_bit[3]), .input_2_1_bit(input2_4_bit[3]),
    .carry_in(full_adder_1_bit_2_carry_out), .carry_out(carry_out), .result(\output [3]));
  full_adder_1_bit full_adder_1_bit_2 (
    .input_1_1_bit(input1_4_bit[2]), .input_2_1_bit(input2_4_bit[2]),
    .carry_in(full_adder_1_bit_3_carry_out), .carry_out(full_adder_1_bit_2_carry_out), .result(\output [2]));
  full_adder_1_bit full_adder_1_bit_3 (
    .input_1_1_bit(input1_4_bit[1]), .input_2_1_bit(input2_4_bit[1]),
    .carry_in(full_adder_1_bit_4_carry_out), .carry_out(full_adder_1_bit_3_carry_out), .result(\output [1]));
  full_adder_1_bit full_adder_1_bit_4 (
    .input_1_1_bit(input1_4_bit[0]), .input_2_1_bit(input2_4_bit[0]), .carry_in(carry_in),
    .carry_out(full_adder_1_bit_4_carry_out), .result(\output [0]));
endmodule

module full_adder_16_bit (
  input  [15:0] input_1_16_bit,
  input  [15:0] input__16_bit,
  input  carry_in,
  output carry_out,
  output [15:0] \output 
);

  wire full_adder_4_bit_2_carry_out, full_adder_4_bit_3_carry_out, full_adder_4_bit_4_carry_out;

  full_adder_4_bit full_adder_4_bit_1 (
    .input1_4_bit(input_1_16_bit[15:12]), .input2_4_bit(input__16_bit[15:12]),
    .carry_in(full_adder_4_bit_2_carry_out), .carry_out(carry_out), .\output (\output [15:12]));
  full_adder_4_bit full_adder_4_bit_2 (
    .input1_4_bit(input_1_16_bit[11:8]), .input2_4_bit(input__16_bit[11:8]),
    .carry_in(full_adder_4_bit_3_carry_out), .carry_out(full_adder_4_bit_2_carry_out),
    .\output (\output [11:8]));
  full_adder_4_bit full_adder_4_bit_3 (
    .input1_4_bit(input_1_16_bit[7:4]), .input2_4_bit(input__16_bit[7:4]),
    .carry_in(full_adder_4_bit_4_carry_out), .carry_out(full_adder_4_bit_3_carry_out),
    .\output (\output [7:4]));
  full_adder_4_bit full_adder_4_bit_4 (
    .input1_4_bit(input_1_16_bit[3:0]), .input2_4_bit(input__16_bit[3:0]), .carry_in(carry_in),
    .carry_out(full_adder_4_bit_4_carry_out), .\output (\output [3:0]));
endmodule

module full_adder_18_bit (
  input  [17:0] in_1,
  input  [17:0] in_2,
  input  [17:0] in_3,
  input  carry_in,
  output carry_out
);

  wire full_adder_1_bit_1_carry_out, full_adder_1_bit_2_carry_out, full_adder_1_bit_3_carry_out,
       full_adder_1_bit_4_carry_out, full_adder_16_bit_2_carry_out;
  wire [15:0] bit_extender_1_out, bit_extender_2_out, full_adder_16_bit_1_output, full_adder_16_bit_2_output;

  assign bit_extender_1_out = {{14{1'b0}}, in_1[1:0]};  // Bit_Extender bit_extender_1
  assign bit_extender_2_out = {{14{1'b0}}, in_3[17:16]};  // Bit_Extender bit_extender_2
  full_adder_16_bit full_adder_16_bit_1 (
    .input_1_16_bit({in_1[3:2], in_1[5:4], in_1[7:6], in_1[9:8], in_1[11:10], in_1[13:12], in_1[15:14], in_1[17:16]}),
    .input__16_bit(bit_extender_1_out), .carry_in(full_adder_1_bit_1_carry_out), .carry_out(carry_out),
    .\output (full_adder_16_bit_1_output));
  full_adder_1_bit full_adder_1_bit_1 (
    .input_1_1_bit(in_1[0]), .input_2_1_bit(in_1[1]), .carry_in(full_adder_1_bit_2_carry_out),
    .carry_out(full_adder_1_bit_1_carry_out));  // open: result
  full_adder_1_bit full_adder_1_bit_2 (
    .input_1_1_bit(in_1[0]), .input_2_1_bit(in_1[1]), .carry_in(full_adder_16_bit_2_carry_out),
    .carry_out(full_adder_1_bit_2_carry_out));  // open: result
  full_adder_16_bit full_adder_16_bit_2 (
    .input_1_16_bit(in_3[15:0]), .input__16_bit(bit_extender_2_out), .carry_in(full_adder_1_bit_3_carry_out),
    .carry_out(full_adder_16_bit_2_carry_out), .\output (full_adder_16_bit_2_output));
  full_adder_1_bit full_adder_1_bit_3 (
    .input_1_1_bit(in_3[16]), .input_2_1_bit(in_3[17]), .carry_in(full_adder_1_bit_4_carry_out),
    .carry_out(full_adder_1_bit_3_carry_out));  // open: result
  full_adder_1_bit full_adder_1_bit_4 (
    .input_1_1_bit(in_3[16]), .input_2_1_bit(in_3[17]), .carry_in(carry_in),
    .carry_out(full_adder_1_bit_4_carry_out));  // open: result
endmodule
